# Fritzing sketch Diagrama (saved by Fritzing 0.9.3b)
breadboards: 1

parts:
  LCD1 = LCD screen
  R1 = Rotary Potentiometer (Small) [maximum_resistance=100kΩ package=THT]
  R2 = Resistor [tolerance=±5% resistance=220 package=THT]
  Componente2 = RFID-RC522-v3
  Componente1 = Arduino Uno (Rev3)
  J1 = Basic Servo

nets:
  GND: LCD1.VSS, R1.leg2, Componente2.GND, Componente1.GND, J1.gnd
  VDD: LCD1.VDD, R1.leg1, R2.Pin_0, Componente1.5V, J1.vcc
  N1: LCD1.V0, R1.wiper
  N2: LCD1.RS, Componente1.D2
  N3: LCD1.E, Componente1.D3_PWM
  N4: LCD1.DB4, Componente1.D4
  N5: LCD1.DB5, Componente1.D5_PWM
  N6: LCD1.DB6, Componente1.D6_PWM
  N7: LCD1.DB7, Componente1.D7
  N8: LCD1.LED+, R2.Pin_1
  N9: Componente2.SDA, Componente1.D10_PWM/SS
  N10: Componente2.SCK, Componente1.D13/SCK
  N11: Componente2.MOSI, Componente1.D11_PWM/MOSI
  N12: Componente2.MISO, Componente1.D12/MISO
  N13: Componente2.RST, Componente1.D9_PWM
  3.3V: Componente2.3.3V, Componente1.3V3
  N14: Componente1.D8, J1.pulse

custom parts:
  RFID-RC522-v3: A simple China made RFID-RC522 Reader (6x4 cm); do check the pin labels, as this is a MFRC522 based clone.
